# Fritzing sketch Weather Station (saved by Fritzing 0.9.3b)
stripboards: 1

parts:
  OLED_I2C1 = OLED 128x64 I2C Monochrome Display  # not connected
  Part1 = Barometric Pressure Sensor - BMP180 Breakout (GY-68)
  S1 = SWITCH_SPDT [package=kps-1290]  # not connected
  U1 = LIPO-110mAh [package=lipo-110]
  Part7 = Micro Lipo Charger
  DHT3 = DHT11 Humitidy and Temperature Sensor
  Part8 = Arduino Pro Mini (3.3V)
  SG2 = Buzzer 12mm [package=buzzer-12mm-ns]

nets (from the schematic view):
  VCC: Part1.VCC, Part1.SCL, Part7.5V, DHT3.VDD, Part8.VCC, Part8.A4
  GND: Part1.GND, Part1.SDA, U1.-, Part7.GND, DHT3.GND, Part8.A5, Part8.GND, SG2.1
  N1: U1.+, Part7.VBAT
  N2: DHT3.DATA, Part8.D2
  N3: Part8.D3, SG2.2

custom parts:
  Micro Lipo Charger: Oh so handy, this little lipo charger is so small and easy to use you can keep it on your desk or mount it easily into any project! Simply plug it via any MicroUSB cable into a USB port and a 3.7V/4.2V lithium polymer or lithium ion rechargeable battery into the JST plug on the other end. There are two LEDs - one red and one green. While charging, the red LED is lit. When the battery is fully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
  DHT11 Humitidy and Temperature Sensor: DHT11 Humidity and Temperature Sensor
